# Fritzing sketch Musicarduino (saved by Fritzing 0.9.3b)
breadboards: 1

parts:
  Arduino_Uno = Arduino Uno (Rev3)
  R1 = Resistor [tolerance=±5% resistance=5.6k package=THT]
  D1 = Rectifier Diode [part_number=1S3 package="300 mil [THT]"]
  L1 = Solenoid [part_number="Sparkfun 5V solenoid"]
  Q1 = NPN-Transistor [part_number=2SC2458-Y package="TO92 [THT]"]
  R2 = Resistor [tolerance=±5% resistance=5.6k package=THT]
  D2 = Rectifier Diode [part_number=1S3 package="300 mil [THT]"]
  L2 = Solenoid [part_number="Sparkfun 5V solenoid"]
  Q2 = NPN-Transistor [part_number=2SC2458-Y package="TO92 [THT]"]
  Q3 = NPN-Transistor [part_number=2SC2458-Y package="TO92 [THT]"]
  L3 = Solenoid [part_number="Sparkfun 5V solenoid"]
  D3 = Rectifier Diode [part_number=1S3 package="300 mil [THT]"]
  D4 = Rectifier Diode [part_number=1S3 package="300 mil [THT]"]
  L4 = Solenoid [part_number="Sparkfun 5V solenoid"]
  Q4 = NPN-Transistor [part_number=2SC2458-Y package="TO92 [THT]"]
  R3 = Resistor [tolerance=±5% resistance=5.6k package=THT]
  R4 = Resistor [tolerance=±5% resistance=5.6k package=THT]
  D5 = Rectifier Diode [part_number=1S3 package="300 mil [THT]"]
  L5 = Solenoid [part_number="Sparkfun 5V solenoid"]
  Q5 = NPN-Transistor [part_number=2SC2458-Y package="TO92 [THT]"]
  R5 = Resistor [tolerance=±5% resistance=5.6k package=THT]
  IC1 = DIP - 24 pins [chip_label=PCA9547D package="DIP (Dual Inline) [THT]"]
  パーツ1 = S11059-02DT  # not connected
  パーツ2 = S11059-02DT  # not connected
  IC2 = IC, DIP package, 8 pins [chip_label=24FC1025-I/P part_number=24FC1025-I/P]  # not connected

nets:
  GND: Arduino_Uno.GND, Q1.E, Q2.E, Q3.E, Q4.E, Q5.E, IC1.pin12
  N1: Arduino_Uno.D2, R1.Pin_0
  N2: Arduino_Uno.D3_PWM, R2.Pin_0
  N3: Arduino_Uno.D4, R3.Pin_0
  N4: Arduino_Uno.D5_PWM, R4.Pin_0
  N5: Arduino_Uno.D6_PWM, R5.Pin_0
  N6: Arduino_Uno.5V, D1.cathode, L1.pin1, D2.cathode, L2.pin1, L3.pin1, D3.cathode, D4.cathode, L4.pin1, D5.cathode, L5.pin1
  N7: R1.Pin_1, Q1.B
  N8: D1.anode, L1.pin2, Q1.C
  N9: R2.Pin_1, Q2.B
  N10: D2.anode, L2.pin2, Q2.C
  N11: Q3.B, R3.Pin_1
  N12: Q3.C, L3.pin2, D3.anode
  N13: D4.anode, L4.pin2, Q4.C
  N14: Q4.B, R4.Pin_1
  N15: D5.anode, L5.pin2, Q5.C
  N16: Q5.B, R5.Pin_1

custom parts:
  DIP - 24 pins: A DIP stand-in part for whatever IC you want. With 24 pins on a 300mil dual inline package (DIP) footprint.
